# Fritzing sketch atalhos_obs (saved by Fritzing 0.9.4)
breadboards: 1

parts:
  S1 = Square Pushbutton
  S2 = Square Pushbutton
  R1 = Resistor [tolerance=±5% resistance=10k package=THT]
  R2 = Resistor [tolerance=±5% resistance=10k package=THT]
  Arduino = Arduino Uno (Rev3)

nets:
  N1: S1.leg0, R1.Pin_1, Arduino.D3_PWM
  N2: S1.leg1, S2.leg1, Arduino.5V
  N3: S2.leg0, R2.Pin_1, Arduino.D2
  N4: R1.Pin_0, R2.Pin_0, Arduino.GND
